# Fritzing sketch Garagentorsteuerung (saved by Fritzing 0.9.10b)
breadboards: 2

parts:
  MH-ET_LIVE_ESP32_DEVKIT1 = MH-ET LIVE ESP32 DEVKIT 38 pins
  U2 = mystery part, 3 pins [chip_label=DS18B20 part_number=DS18B20]
  LED3 = LED - 5mm [color="Green (565nm)" current=0.030 package="5 mm [THT]"]
  LED4 = LED - 5mm [color="Red (633nm)" current=0.030 package="5 mm [THT]"]
  R5 = Resistor [tolerance=±5% power=0.25 resistance=220 package=THT]
  R6 = Resistor [tolerance=±5% power=0.25 resistance=220 package=THT]
  M1 = AC-05-03
  R4 = Resistor [tolerance=±5% power=0.25 resistance=4.7k package=THT]
  Bauteil2 = I2C level shifter bidirectional
  LED5 = LED - 5mm [color="Orange (612nm)" current=0.030 package="5 mm [THT]"]
  R7 = Resistor [tolerance=±5% power=0.25 resistance=220 package=THT]
  J4 = female pin header, 3 pins [form="♀ (female)"]
  C1 = Ceramic Capacitor [capacitance=1nF voltage=35V package="100 mil [THT, multilayer]"]
  IC1 = IC, DIP package, 16 pins [chip_label=MC14490P]
  C2 = Ceramic Capacitor [capacitance=10nF voltage=35V package="100 mil [THT, multilayer]"]
  C3 = Ceramic Capacitor [capacitance=100nF voltage=35V package="100 mil [THT, multilayer]"]
  S1 = Reed switch [package=THT]
  S2 = Reed switch [package=THT]
  S3 = Reed switch [package=THT]
  S4 = Reed switch [package=THT]

nets:
  N1: MH-ET_LIVE_ESP32_DEVKIT1.3V3, U2.pin3, R4.Pin_1, Bauteil2.LV, IC1.pin16, C2.0, C3.0
  N2: MH-ET_LIVE_ESP32_DEVKIT1.IO32, IC1.pin15
  N3: MH-ET_LIVE_ESP32_DEVKIT1.IO33, IC1.pin2
  N4: MH-ET_LIVE_ESP32_DEVKIT1.IO25, U2.pin2, R4.Pin_0
  N5: MH-ET_LIVE_ESP32_DEVKIT1.IO26, IC1.pin13
  N6: MH-ET_LIVE_ESP32_DEVKIT1.IO27, IC1.pin4
  N7: MH-ET_LIVE_ESP32_DEVKIT1.5V, M1.pin_3, Bauteil2.HV, J4.pin3
  N8: MH-ET_LIVE_ESP32_DEVKIT1.GND#64, U2.pin1, LED3.cathode, LED4.cathode, M1.pin_4, Bauteil2.GND, LED5.cathode, J4.pin2, IC1.pin8, C2.1, C3.1, S1.pin_1, S2.pin_1, S3.pin_1, S4.pin_1
  N9: MH-ET_LIVE_ESP32_DEVKIT1.IO23, R5.Pin_0
  N10: MH-ET_LIVE_ESP32_DEVKIT1.IO22, R7.Pin_0
  N11: MH-ET_LIVE_ESP32_DEVKIT1.IO19, R6.Pin_0
  N12: MH-ET_LIVE_ESP32_DEVKIT1.IO18, Bauteil2.LV1
  N13: LED3.anode, R6.Pin_1
  N14: LED4.anode, R5.Pin_1
  N15: Bauteil2.HV1, J4.pin1
  N16: LED5.anode, R7.Pin_1
  N17: C1.0, IC1.pin7
  N18: C1.1, IC1.pin9
  N19: IC1.pin1, S3.pin_2
  N20: IC1.pin3, S1.pin_2
  N21: IC1.pin12, S4.pin_2
  N22: IC1.pin14, S2.pin_2

notes:
  Schaltkanal über Relais (CHN2|DC-|DC+) (5V)
  Spannungsversorgung über AC-05-03

custom parts:
  MH-ET LIVE ESP32 DEVKIT 38 pins: http://mh.nodebb.com/topic/2/mh-et-live-esp32-devkit
  AC-05-03: AC-DC 220V to 5V Step-Down Power Supply Module
